# Fritzing sketch no atuador relatorio1 (saved by Fritzing 0.9.2b)
breadboards: 1

parts:
  Part1 = Arduino Uno (Rev3)  # not connected
  Part2 = Arduino Ethernet Shield (Rev3)
  L1 = Solenoid
  U2 = RELAY [package=relay-jzc]
  U3 = RELAY [package=relay-jzc]
  U4 = RELAY [package=relay-jzc]
  U5 = RELAY [package=relay-jzc]

nets:
  N1: Part2.TX/D1, U5.NC
  N2: Part2.D2, U4.NC
  N3: Part2.PWM_D3, U3.NC
  N4: Part2.SDCS, U2.NC
  N5: Part2.5V, U5.NO
  N6: Part2.GND, U5.COIL2
  N7: L1.pin2, U2.COIL1

notes:
  FAN
  Lamp 1
  Lamp 2
  220 V
