# Fritzing sketch no sensor relatorio 1 IOT (saved by Fritzing 0.9.2b)
breadboards: 1

parts:
  Part1 = Arduino Uno (Rev3)
  Part2 = Arduino Ethernet Shield (Rev3)
  T1 = TMP36 Temperature Sensor [package="TO92 [THT]"]
  R1 = Photocell (LDR) [package=THT]
  R2 = Resistor [tolerance=±5% resistance=10k package="0603 [SMD]"]

nets:
  N1: Part1.5V, T1.+Vs, R2.Pin_1
  N2: Part2.A0, R1.pin_1, R2.Pin_0
  N3: Part2.A1, T1.Vout
  GND: Part2.GND, T1.GND, R1.pin_0
